# Fritzing sketch electronics (saved by Fritzing 1.0.3b)
breadboards: 1

parts:
  U2 = ESP32S-HiLetgo [part_number=ESP32S-HiLetgo]  # not connected
  VCC2 = Battery block 9V [internal_resistance=0.1Ω]
  A2 = mini560 [package=THT]
  Part2 = SparkFun Motor Driver TB6612FNG (v11) [part_number=ROB-14451]  # not connected
  M4 = DC Motor [voltage_(max)=6V voltage_(min)=3V]  # not connected
  M5 = DC Motor [voltage_(max)=6V voltage_(min)=3V]  # not connected
  M6 = fc-51 [package=THT]  # not connected
  M7 = fc-51 [package=THT]  # not connected
  J2 = Infrared Proximity Sensor [distance_to_obstacle=50%]  # not connected
  S1 = 0.91 inch OLED I2C Display 128 x 32 Pixels  # not connected

nets:
  N1: VCC2.-, A2.pin_3, A2.pin_7
  N2: VCC2.+, A2.pin_1

custom parts:
  ESP32S-HiLetgo: HiLetgo ESP-WROOM-32 ESP32 ESP-32S Development Board 2.4GHz Dual-Mode WiFi + Bluetooth Dual Cores Microcontroller The ESP32 integrated with Antenna switches, RF Balun, power amplifiers, low-noise amplifiers, filters, and management modules, and the entire solution occupies the least area of PCB. 2.4 GHz Wi-Fi plus Bluetooth dual-mode chip, with TSMC Ultra-low power consumption 40nm technology,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
  mini560: 5A DC-DC Mini 560 Step Down Stabilized Voltage Supply Module Output 3.3 5V 9V 12V Step-down Power Converter Board Module
  SparkFun Motor Driver TB6612FNG (v11): The TB6612FNG Motor Driver can control up to two DC motors at a constant current of 1.2A (3.2A peak). Two input signals (IN1 and IN2) can be used to control the motor in one of four function modes: CW, CCW, short-brake and stop. The two motor outputs (A and B) can be separately controlled, and the speed of each motor is controlled via a PWM input signal with a frequency up to 100kHz. The STBY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
